# Fritzing sketch wiring-diagram (saved by Fritzing 0.9.3b)

parts:
  Part1 = Adafruit Feather nRF52 [part_number="Adafruit #3406"]
  S1 = Toggle Switch [package=THT]
  DC_Mot_Enc1 = DC Motor with two-phase hall-encoder [part_number=VT-E-G25A-06-177E]
  Part2 = DRV8835 Dual Motor Driver Carrier
  DC_Mot_Enc2 = DC Motor with two-phase hall-encoder [part_number=VT-E-G25A-06-177E]
  Part3 = Lithium Ion Polymer Battery 3.7v 150mAh [part_number=1317]
  J3 = JST-03JQ-BT [part_number=JST-JQ-BT package=THT]
  R1 = Resistor [tolerance=±5% resistance=220 package="0603 [SMD]"]

nets:
  3.3V: Part1.3.3V, DC_Mot_Enc1.pin2, Part2.VCC, DC_Mot_Enc2.pin2, R1.Pin_0
  N1: Part1.GND, DC_Mot_Enc1.pin5, Part2.GND#0, DC_Mot_Enc2.pin5
  N2: Part1.A0/0.02, Part2.BIN2/BENABLE, Part2.AOUT1, DC_Mot_Enc2.pin6
  N3: Part1.A1/0.03, Part2.AIN2/AENABLE
  N4: Part1.A2/0.04, DC_Mot_Enc1.pin4
  N5: Part1.A3/0.05, DC_Mot_Enc1.pin3
  N6: Part1.A4/0.28, DC_Mot_Enc2.pin4
  N7: Part1.A5/0.29, DC_Mot_Enc2.pin3
  N8: Part1.P0.15, Part2.BIN1/BPHASE
  N9: Part1.P0.16, Part2.AIN1/APHASE
  N10: S1.L1, Part3.positive
  N11: S1.COM, Part2.VIN, J3.pin3
  N12: DC_Mot_Enc1.pin1, Part2.BOUT2
  N13: DC_Mot_Enc1.pin6, Part2.BOUT1
  N14: Part2.MODE, R1.Pin_1
  N15: Part2.AOUT2, DC_Mot_Enc2.pin1
  N16: Part2.GND#14, Part3.negative, J3.pin1

custom parts:
  Lithium Ion Polymer Battery 3.7v 150mAh: Lithium ion polymer (also known as 'lipo' or 'lipoly') batteries are thin, light and powerful. The output ranges from 4.2V when completely charged to 3.7V. This battery has a capacity of 150mAh for a total of about 0.6 Wh. The batteries come pre-attached with a genuine 2-pin JST-PH connector as shown and include the necessary protection circuitry.
